# Fritzing sketch схема (saved by Fritzing 0.9.3b)
breadboards: 2

parts:
  Часть1 = Arduino Nano (Rev3.0)
  Q1 = NPN-Transistor [package="TO92 [THT]"]
  S1 = Pushbutton [package="[THT]"]
  S2 = Pushbutton [package="[THT]"]
  J1 = Piezo Speaker
  Disp1 = LBT2088AH [part_number=LBT2088AH]

nets:
  N1: Часть1.D2, Q1.B
  N2: Часть1.D5, Disp1.pin_7
  N3: Q1.E, J1.pin2
  N4: Q1.C, Disp1.pin_6
  N5: S1.Pin_3, S2.Pin_3, J1.pin1, Disp1.pin_8
